// Logisim project binary project no segments just bits.circ as structural Verilog: 1 circuit, main circuit main
module main (
  input  in_1,
  output out_2,
  output out_3,
  output out_4,
  output out_5
);

  wire and_1_out, and_2_out, and_3_out, and_4_out, and_5_out, and_6_out, and_7_out, and_8_out, and_9_out,
       and_10_out, and_11_out, and_12_out, and_13_out, and_14_out, and_15_out, and_16_out, clock_1_out,
       not_1_out, not_2_out, not_3_out, not_4_out, not_5_out, or_1_out, or_2_out, or_3_out, or_4_out,
       or_5_out, or_6_out, or_7_out;

  not not_1 (not_1_out, in_1);
  not not_2 (not_2_out, out_2);
  not not_3 (not_3_out, out_3);
  not not_4 (not_4_out, out_4);
  not not_5 (not_5_out, out_5);
  Clock clock_1 (.out(clock_1_out));
  and and_1 (and_1_out, not_1_out, out_3, out_4, not_5_out);
  or or_1 (or_1_out, and_1_out, and_2_out);
  and and_2 (and_2_out, out_5, not_4_out, not_3_out, in_1);
  and and_3 (and_3_out, not_5_out, out_4, out_3, not_1_out);
  or or_2 (or_2_out, and_3_out, and_4_out);
  and and_4 (and_4_out, out_5, not_4_out, not_3_out, in_1);
  and and_5 (and_5_out, out_3, not_4_out);
  and and_6 (and_6_out, out_3, out_5);
  or or_3 (or_3_out, and_5_out, and_6_out, and_7_out);
  and and_7 (and_7_out, not_3_out, out_4, not_5_out);
  and and_8 (and_8_out, out_3, not_5_out);
  and and_9 (and_9_out, out_3, out_4);
  or or_4 (or_4_out, and_8_out, and_9_out, and_10_out);
  and and_10 (and_10_out, not_3_out, not_4_out, out_5);
  and and_11 (and_11_out, not_4_out, not_1_out);
  or or_5 (or_5_out, and_11_out, and_12_out);
  and and_12 (and_12_out, in_1, not_4_out);
  and and_13 (and_13_out, not_1_out, out_4);
  or or_6 (or_6_out, and_13_out, and_14_out);
  and and_14 (and_14_out, not_4_out, in_1);
  and and_15 (and_15_out, or_3_out, not_1_out);
  or or_7 (or_7_out, and_15_out, and_16_out);
  and and_16 (and_16_out, or_4_out, in_1);
  D_Flip_Flop d_ff_1 (.clk(clock_1_out), .D(or_5_out), .Q(out_4));  // open: Qn, preset, en, reset
  T_Flip_Flop t_ff_1 (.clk(clock_1_out), .T(or_6_out), .Q(out_5));  // open: Qn, preset, reset, en
  J_K_Flip_Flop j_k_ff_1 (.J(or_1_out), .clk(clock_1_out), .K(or_2_out), .Q(out_2));  // open: Qn, preset, en, reset
  D_Flip_Flop d_ff_2 (.clk(clock_1_out), .D(or_7_out), .Q(out_3));  // open: Qn, preset, en, reset
endmodule
